// Logisim project cofreprogramavelfinal.circ as structural Verilog: 4 circuits, main circuit main
module main (
  input  Set_Password
);

  wire _0, _1, _2, _3, _4, _5, _6, _7, _8, _9, and_1_out, b0, b1, b2, b3, D1, D2, D3, D4, m1b0, m1b1, m1b2,
       m1b3, m2b0, m2b1, m2b2, m2b3, m3b0, m3b1, m3b2, m3b3, m4b0, m4b1, m4b2, m4b3, memoriasenha_1_sm1b0,
       memoriasenha_1_sm1b1, memoriasenha_1_sm1b2, memoriasenha_1_sm1b3, memoriasenha_1_sm2b0,
       memoriasenha_1_sm2b1, memoriasenha_1_sm2b2, memoriasenha_1_sm2b3, memoriasenha_1_sm3b0,
       memoriasenha_1_sm3b1, memoriasenha_1_sm3b2, memoriasenha_1_sm3b3, memoriasenha_1_sm4b0,
       memoriasenha_1_sm4b1, memoriasenha_1_sm4b2, memoriasenha_1_sm4b3, xor_1_out, xor_2_out, xor_3_out,
       xor_4_out, xor_5_out, xor_6_out, xor_7_out, xor_8_out, xor_9_out, xor_10_out, xor_11_out, xor_12_out,
       xor_13_out, xor_14_out, xor_15_out, xor_16_out;

  memorias memorias_1 (
    .b3(b3), .b2(b2), .b1(b1), .b0(b0), .m1b3(m1b3), .m2b3(m2b3), .m3b3(m3b3), .m4b3(m4b3), .m1b2(m1b2),
    .m2b2(m2b2), .m3b2(m3b2), .m4b2(m4b2), .m1b1(m1b1), .m2b1(m2b1), .m3b1(m3b1), .m4b1(m4b1), .m1b0(m1b0),
    .m2b0(m2b0), .m3b0(m3b0), .m4b0(m4b0), ._0(_0));
  DectoBinconverter dectobinconverter_1 (
    ._0(_0), ._1(_1), ._2(_2), ._3(_3), ._4(_4), ._5(_5), ._6(_6), ._7(_7), ._8(_8), ._9(_9), .b3(b3),
    .b2(b2), .b1(b1), .b0(b0));
  // Probe on b3
  // Probe on b2
  // Probe on b1
  // Probe on b0
  Button u__7 (.out(_7));
  Button u__8 (.out(_8));
  Button u__4 (.out(_4));
  Button u__5 (.out(_5));
  Button u__1 (.out(_1));
  Button u__2 (.out(_2));
  Button u__0 (.out(_0));
  Button u__9 (.out(_9));
  Button u__6 (.out(_6));
  Button u__3 (.out(_3));
  LED led_1 (.in(D1));
  LED led_2 (.in(D2));
  LED led_3 (.in(D3));
  LED led_4 (.in(D4));
  and and_1 (and_1_out, D1, D2, D3, D4);
  memoriasenha memoriasenha_1 (
    ._0(_0), .b3(b3), .b2(b2), .b1(b1), .b0(b0), .programar(Set_Password), .sm1b3(memoriasenha_1_sm1b3),
    .sm2b3(memoriasenha_1_sm2b3), .sm3b3(memoriasenha_1_sm3b3), .sm4b3(memoriasenha_1_sm4b3),
    .sm1b2(memoriasenha_1_sm1b2), .sm2b2(memoriasenha_1_sm2b2), .sm3b2(memoriasenha_1_sm3b2),
    .sm4b2(memoriasenha_1_sm4b2), .sm1b1(memoriasenha_1_sm1b1), .sm2b1(memoriasenha_1_sm2b1),
    .sm3b1(memoriasenha_1_sm3b1), .sm4b1(memoriasenha_1_sm4b1), .sm1b0(memoriasenha_1_sm1b0),
    .sm2b0(memoriasenha_1_sm2b0), .sm3b0(memoriasenha_1_sm3b0), .sm4b0(memoriasenha_1_sm4b0));
  LED safe_unlocked (.in(and_1_out));
  xor xor_1 (xor_1_out, m1b3, memoriasenha_1_sm1b3);
  xor xor_2 (xor_2_out, m1b2, memoriasenha_1_sm1b2);
  nor nor_1 (D1, xor_1_out, xor_2_out, xor_3_out, xor_4_out);
  xor xor_3 (xor_3_out, m1b1, memoriasenha_1_sm1b1);
  xor xor_4 (xor_4_out, m1b0, memoriasenha_1_sm1b0);
  xor xor_5 (xor_5_out, m2b3, memoriasenha_1_sm2b3);
  xor xor_6 (xor_6_out, m2b2, memoriasenha_1_sm2b2);
  xor xor_7 (xor_7_out, m2b1, memoriasenha_1_sm2b1);
  nor nor_2 (D2, xor_5_out, xor_6_out, xor_7_out, xor_8_out);
  xor xor_8 (xor_8_out, m2b0, memoriasenha_1_sm2b0);
  xor xor_9 (xor_9_out, m3b3, memoriasenha_1_sm3b3);
  xor xor_10 (xor_10_out, m3b2, memoriasenha_1_sm3b2);
  nor nor_3 (D3, xor_9_out, xor_10_out, xor_12_out, xor_11_out);
  xor xor_11 (xor_11_out, m3b0, memoriasenha_1_sm3b0);
  xor xor_12 (xor_12_out, m3b1, memoriasenha_1_sm3b1);
  xor xor_13 (xor_13_out, m4b3, memoriasenha_1_sm4b3);
  xor xor_14 (xor_14_out, m4b2, memoriasenha_1_sm4b2);
  xor xor_15 (xor_15_out, m4b1, memoriasenha_1_sm4b1);
  nor nor_4 (D4, xor_13_out, xor_14_out, xor_15_out, xor_16_out);
  xor xor_16 (xor_16_out, m4b0, memoriasenha_1_sm4b0);
endmodule

module DectoBinconverter (
  input  _0,
  input  _1,
  input  _2,
  input  _3,
  input  _4,
  input  _5,
  input  _6,
  input  _7,
  input  _8,
  input  _9,
  output b3,
  output b2,
  output b1,
  output b0
);

  or or_1 (b3, _8, _9);
  or or_2 (b2, _7, _6, _5, _4);
  or or_3 (b1, _2, _3, _7, _6);
  or or_4 (b0, _1, _3, _5, _7, _9);
endmodule

module memorias (
  input  _0,
  input  b3,
  input  b2,
  input  b1,
  input  b0,
  output m1b3,
  output m2b3,
  output m3b3,
  output m4b3,
  output m1b2,
  output m2b2,
  output m3b2,
  output m4b2,
  output m1b1,
  output m2b1,
  output m3b1,
  output m4b1,
  output m1b0,
  output m2b0,
  output m3b0,
  output m4b0
);

  wire or_1_out;

  or or_1 (or_1_out, b3, b2, _0, b1, b0);
  D_Flip_Flop d_ff_1 (.clk(or_1_out), .D(b3), .Q(m1b3));  // open: Qn, preset, en, reset
  D_Flip_Flop d_ff_2 (.clk(or_1_out), .D(b2), .Q(m1b2));  // open: Qn, preset, en, reset
  D_Flip_Flop d_ff_3 (.clk(or_1_out), .D(b1), .Q(m1b1));  // open: Qn, preset, en, reset
  D_Flip_Flop d_ff_4 (.clk(or_1_out), .D(b0), .Q(m1b0));  // open: Qn, preset, en, reset
  D_Flip_Flop d_ff_5 (.clk(or_1_out), .D(m1b3), .Q(m2b3));  // open: Qn, preset, en, reset
  D_Flip_Flop d_ff_6 (.clk(or_1_out), .D(m1b2), .Q(m2b2));  // open: Qn, preset, en, reset
  D_Flip_Flop d_ff_7 (.clk(or_1_out), .D(m1b1), .Q(m2b1));  // open: Qn, preset, en, reset
  D_Flip_Flop d_ff_8 (.clk(or_1_out), .D(m1b0), .Q(m2b0));  // open: Qn, preset, en, reset
  D_Flip_Flop d_ff_9 (.clk(or_1_out), .D(m2b3), .Q(m3b3));  // open: Qn, preset, en, reset
  D_Flip_Flop d_ff_10 (.clk(or_1_out), .D(m2b2), .Q(m3b2));  // open: Qn, preset, en, reset
  D_Flip_Flop d_ff_11 (.clk(or_1_out), .D(m2b1), .Q(m3b1));  // open: Qn, preset, en, reset
  D_Flip_Flop d_ff_12 (.clk(or_1_out), .D(m2b0), .Q(m3b0));  // open: Qn, preset, en, reset
  D_Flip_Flop d_ff_13 (.clk(or_1_out), .D(m3b3), .Q(m4b3));  // open: Qn, preset, en, reset
  D_Flip_Flop d_ff_14 (.clk(or_1_out), .D(m3b2), .Q(m4b2));  // open: Qn, preset, en, reset
  D_Flip_Flop d_ff_15 (.clk(or_1_out), .D(m3b1), .Q(m4b1));  // open: Qn, preset, en, reset
  D_Flip_Flop d_ff_16 (.clk(or_1_out), .D(m3b0), .Q(m4b0));  // open: Qn, preset, en, reset
endmodule

module memoriasenha (
  input  _0,
  input  b3,
  input  b2,
  input  b1,
  input  b0,
  input  programar,
  output sm1b3,
  output sm2b3,
  output sm3b3,
  output sm4b3,
  output sm1b2,
  output sm2b2,
  output sm3b2,
  output sm4b2,
  output sm1b1,
  output sm2b1,
  output sm3b1,
  output sm4b1,
  output sm1b0,
  output sm2b0,
  output sm3b0,
  output sm4b0
);

  wire or_1_out;

  or or_1 (or_1_out, b3, b2, _0, b1, b0);
  D_Flip_Flop d_ff_1 (.clk(or_1_out), .D(b3), .Q(sm1b3), .en(programar));  // open: Qn, preset, reset
  D_Flip_Flop d_ff_2 (.clk(or_1_out), .D(b2), .Q(sm1b2), .en(programar));  // open: Qn, preset, reset
  D_Flip_Flop d_ff_3 (.clk(or_1_out), .D(b1), .Q(sm1b1), .en(programar));  // open: Qn, preset, reset
  D_Flip_Flop d_ff_4 (.clk(or_1_out), .D(b0), .Q(sm1b0), .en(programar));  // open: Qn, preset, reset
  D_Flip_Flop d_ff_5 (.clk(or_1_out), .D(sm1b3), .Q(sm2b3), .en(programar));  // open: Qn, preset, reset
  D_Flip_Flop d_ff_6 (.clk(or_1_out), .D(sm1b2), .Q(sm2b2), .en(programar));  // open: Qn, preset, reset
  D_Flip_Flop d_ff_7 (.clk(or_1_out), .D(sm1b1), .Q(sm2b1), .en(programar));  // open: Qn, preset, reset
  D_Flip_Flop d_ff_8 (.clk(or_1_out), .D(sm1b0), .Q(sm2b0), .en(programar));  // open: Qn, preset, reset
  D_Flip_Flop d_ff_9 (.clk(or_1_out), .D(sm2b3), .Q(sm3b3), .en(programar));  // open: Qn, preset, reset
  D_Flip_Flop d_ff_10 (.clk(or_1_out), .D(sm2b2), .Q(sm3b2), .en(programar));  // open: Qn, preset, reset
  D_Flip_Flop d_ff_11 (.clk(or_1_out), .D(sm2b1), .Q(sm3b1), .en(programar));  // open: Qn, preset, reset
  D_Flip_Flop d_ff_12 (.clk(or_1_out), .D(sm2b0), .Q(sm3b0), .en(programar));  // open: Qn, preset, reset
  D_Flip_Flop d_ff_13 (.clk(or_1_out), .D(sm3b3), .Q(sm4b3), .en(programar));  // open: Qn, preset, reset
  D_Flip_Flop d_ff_14 (.clk(or_1_out), .D(sm3b2), .Q(sm4b2), .en(programar));  // open: Qn, preset, reset
  D_Flip_Flop d_ff_15 (.clk(or_1_out), .D(sm3b1), .Q(sm4b1), .en(programar));  // open: Qn, preset, reset
  D_Flip_Flop d_ff_16 (.clk(or_1_out), .D(sm3b0), .Q(sm4b0), .en(programar));  // open: Qn, preset, reset
endmodule
